# Fritzing sketch Swiecimy (saved by Fritzing 0.9.3b)
breadboards: 1

parts:
  Raspberry_Pi1 = Raspberry Pi 2
  LED_1 = smd LED [color="Red (633nm)" package="1206 [SMD]"]
  R1 = Resistor [tolerance=±5% resistance=330 package="2010 [SMD]"]

nets:
  N1: Raspberry_Pi1.GPIO4, LED_1.anode
  N2: Raspberry_Pi1.GND, R1.Pin_0
  N3: LED_1.cathode, R1.Pin_1

// code stored in the sketch: Untitled3.ino
import RPi.GPIO as GPIO
import time
