# Fritzing sketch servo (saved by Fritzing 0.9.3b)

parts:
  Raspberry_Pi1 = Raspberry Pi 2
  J1 = Basic Servo

nets:
  GND: Raspberry_Pi1.GND, J1.gnd
  N1: Raspberry_Pi1.GPIO23, J1.pulse
  5V: Raspberry_Pi1.5V, J1.vcc
