# Fritzing sketch PWM (saved by Fritzing 0.9.3b)
breadboards: 1

parts:
  R1 = Resistor [tolerance=±5% resistance=330 package=THT]
  LED1 = LED - 5mm [color="Red (633nm)" package="5 mm [THT]"]
  Raspberry_Pi1 = Raspberry Pi 2

nets:
  N1: R1.Pin_0, Raspberry_Pi1.GND
  N2: R1.Pin_1, LED1.cathode
  N3: LED1.anode, Raspberry_Pi1.GPIO17
